// Logisim project 1241_display.circ as structural Verilog: 4 circuits, main circuit display
module display (
  input  [7:0] ID,
  input  [13:0] IA,
  input  RD_L,
  input  IWR_L,
  input  DREG_L,
  input  CROM_L,
  output VIDEO,
  output HDRIVE_L,
  output CLK_2_4_MHz,
  output VDRIVE_GREEN,
  output VLATCH,
  output CLK_9_8_MHz_L,
  output IWAIT_L,
  output CSYNC_CROM_L
);

  wire BIT0, BIT1, BUF_L, CB, CB_L, CLK_1_2_MHz, CLK_2_4_MHz_L, CLK_2_4_MHz_t, CLK_4_8_MHz, CLK_9_8_MHz,
       CLK_19_6_MHz, DROM_L, EXPM, G0, G_0, GT_BLNK, GTMODE, GTMODE_L, HD, HSEL_L, IDP_LOCKOUT, INDEX_L,
       LATCH_200_L, LCP, LOADC_L, LOE_L, nand_1_out, nor_1_out, not_1_out, not_2_out, OE_L, PRE_GT_BLNK_L,
       Q_1, T1, T_1, TMODE_L, ttl_74163_1_rco, ttl_74166_1_qh, ttl_74279_sr_1_q, U100A_out, U100B_out,
       U100C_out, U105D_out, U108A_out, U108B_out, U108C_out, U108D_out, U110A_out, U110C_out, U110F_out,
       U115B_out, U115C_out, U115D_out, U120_y1, U120_y2, U120_y3, U120_y4, U125_q1, U125_q2, U125_q3,
       U125_q4, U125_q5, U125_q6, U125_q7, U140_q1, U140_q2, U140_q3, U140_q4, U140_q5, U140_q6, U140_q7,
       U140_q8, U170A_out, U170B_out, U170D_out, U185_q1, U185_q2, U185_q3, U185_q4, U190_c4, U195_q1,
       U195_q2, U195_q3, U195_q4, U198_qc, U198_qd, U198_rco, U200A_nq, U200B_nq, U205B_out, U205C_out,
       U208D_out, U208F_out, U210A_out, U210B_out, U210C_out, U220_q5, U220_q7, U225_q1, U225_q2, U225_q3,
       U225_q4, U225_q5, U225_q6, U225_q7, U225_q8, U230_b1, U230_b2, U230_b3, U235_b1, U235_b2, U265A_out,
       U265C_out, U265D_out, U270A_out, U270B_out, U270C_out, U275A_out, U275B_out, U275D_out, U285_q1,
       U285_q2, U285_q3, U285_q4, U290_c4, U295_q1, U295_q4, U298_rco, U305A_nq, U305A_q, U305B_nq, U305B_q,
       U308A_q, U308B_nq, U310A_out, U310B_out, U310C_out, U310D_out, U405A_out, U405C_out, U405E_out,
       U405F_out, U408_y11, U408_y13, U408_y14, U408_y23, U408_y24, U410C_out, U410E_out, U415B_q, U420_nq1,
       U420_nq2, U420_nq3, U420_nq4, U420_q1, U420_q2, U420_q4, U435A_nq, U435A_q, U480A_q, U480C_q,
       U495A_out, U560_qa0, U560_qa1, U560_qa2, U560_qa3, U560_qb0, U560_qb1, U560_qb2, U560_qb3, undriven,
       undriven_2, undriven_3, undriven_4, undriven_5, undriven_6, undriven_7, undriven_8, undriven_9,
       VRES_L, VSEL_L, YG490_out;
  wire [2:0] L;
  wire [6:2] U240_q3;
  wire [7:0] R, U130_d0, U230_b0, Y;
  wire [7:3] U240_q4;
  wire [10:0] U298_qa;
  wire [11:0] U260_y4;

  Clock YG490 (.out(YG490_out));
  nand nand_1 (nand_1_out, GTMODE, EXPM);
  // NoConnect on undriven
  // NoConnect on undriven_2
  not U495B (CLK_19_6_MHz, YG490_out);
  not U495A (U495A_out, LATCH_200_L);
  not not_1 (not_1_out, Q_1);
  ttl_74670 U295 (
    .Q1(U295_q1), .Q2(BIT1), .Q3(BIT0), .Q4(U295_q4), .RA(GTMODE), .RB(CLK_2_4_MHz_t), .GR(1'b0), .D2(ID[1]),
    .D3(ID[2]), .D4(ID[3]), .WA(IA[0]), .WB(IA[1]), .GW(HSEL_L), .D1(ID[0]));
  or U105D (U105D_out, TMODE_L, CLK_2_4_MHz_L);
  ttl_74157 U260 (
    .Y1(U260_y4[3]), .Y2(U260_y4[2]), .Y3(U260_y4[1]), .Y4(U260_y4[0]), .STROBE(1'b0), .SEL(U170D_out),
    .B1(IA[3]), .A2(U298_qa[2]), .B2(IA[2]), .A3(U298_qa[1]), .B3(IA[1]), .A4(U298_qa[0]), .B4(IA[0]),
    .A1(U298_qa[3]));
  // NoConnect on U120_y4
  ttl_74157 U120 (
    .Y1(U120_y1), .Y2(U120_y2), .Y3(U120_y3), .Y4(U120_y4), .STROBE(1'b0), .SEL(nand_1_out), .B1(L[2]),
    .A2(R[2]), .B2(L[1]), .A3(R[1]), .B3(L[0]), .A4(undriven_2), .B4(undriven), .A1(R[3]));
  or U405A (U405A_out, GT_BLNK, CB);
  // NoConnect on undriven_3
  // NoConnect on undriven_4
  // NoConnect on undriven_5
  // NoConnect on undriven_6
  and U108B (U108B_out, RD_L, IWR_L);
  and U170A (U170A_out, U298_qa[10], U105D_out);
  ttl_74273 U140 (
    .Q1(U140_q1), .Q2(U140_q2), .Q3(U140_q3), .Q4(U140_q4), .Q5(U140_q5), .Q6(U140_q6), .Q7(U140_q7),
    .Q8(U140_q8), .CLK(CLK_2_4_MHz_t), .CLR(1'b1), .D1(Y[0]), .D2(Y[1]), .D3(Y[2]), .D4(Y[3]), .D5(Y[4]),
    .D6(Y[5]), .D7(Y[6]), .D8(Y[7]));
  nand U270A (U270A_out, R[5], R[4], U495A_out);
  or U115B (U115B_out, R[5], U420_nq3);
  or U405E (U405E_out, IDP_LOCKOUT, U108B_out);
  ttl_74175 U420 (
    .NQ1(U420_nq1), .Q2(U420_q2), .NQ2(U420_nq2), .Q3(EXPM), .NQ3(U420_nq3), .Q4(U420_q4), .NQ4(U420_nq4),
    .Q1(U420_q1), .CLR(1'b1), .CLK(DREG_L), .D2(ID[1]), .D3(ID[2]), .D4(ID[3]), .D1(ID[0]));
  // NoConnect on U420_nq2
  // NoConnect on U420_nq4
  ttl_74139 U408 (
    .Y14(U408_y14), .Y21(HSEL_L), .Y22(VSEL_L), .Y23(U408_y23), .Y24(U408_y24), .Y11(U408_y11), .Y12(DROM_L),
    .Y13(U408_y13), .A1(IA[13]), .B1(U420_q4), .G2(U408_y11), .A2(IA[11]), .B2(IA[12]), .G1(CROM_L));
  ttl_74393 U280 (
    .QA0(R[0]), .QA1(R[1]), .QA2(R[2]), .QA3(R[3]), .QB0(R[4]), .QB1(R[5]), .QB2(R[6]), .QB3(R[7]),
    .CLR_A(1'b0), .CLK_A(HDRIVE_L), .CLR_B(1'b0), .CLK_B(R[3]));
  ttl_74163 U298 (
    .QA(U298_qa[0]), .QB(U298_qa[1]), .QC(U298_qa[2]), .QD(U298_qa[3]), .RCO(U298_rco), .ENP(1'b1),
    .ENT(1'b1), .CLR(not_1_out), .LD(nor_1_out), .CLK(CLK_2_4_MHz_t), .A(U295_q1), .B(BIT1), .C(BIT0),
    .D(U295_q4));
  // NoConnect on ttl_74163_1_rco
  ttl_74163 ttl_74163_1 (
    .QA(CLK_9_8_MHz), .QB(CLK_4_8_MHz), .QC(CLK_2_4_MHz_t), .QD(CLK_1_2_MHz), .RCO(ttl_74163_1_rco),
    .ENP(1'b1), .ENT(1'b1), .CLR(1'b1), .LD(1'b1), .CLK(CLK_19_6_MHz), .A(undriven_3), .B(undriven_4),
    .C(undriven_5), .D(undriven_6));
  rom_char U130 (
    .D0(U130_d0[0]), .D1(U130_d0[1]), .D2(U130_d0[2]), .D3(U130_d0[3]), .D4(U130_d0[4]), .D5(U130_d0[5]),
    .D6(U130_d0[6]), .D7(U130_d0[7]), .CE(1'b0), .A0(U120_y3), .A1(U120_y2), .A2(U120_y1), .A3(U140_q1),
    .A4(U140_q2), .A5(U140_q3), .A6(U140_q4), .A7(U140_q5), .A8(U140_q6), .A9(U140_q7), .A10(U140_q8),
    .A11(GTMODE), .OE(1'b0));
  not U410E (U410E_out, U115B_out);
  xor U310C (U310C_out, U420_q1, CLK_9_8_MHz);
  and U170B (U170B_out, GTMODE, CLK_2_4_MHz_t);
  and U170D (U170D_out, CLK_2_4_MHz_L, GTMODE_L);
  ttl_74157 U165 (
    .Y1(U260_y4[10]), .Y2(U260_y4[5]), .Y3(U260_y4[4]), .Y4(U260_y4[11]), .STROBE(1'b0), .SEL(U170D_out),
    .B1(IA[10]), .A2(U298_qa[5]), .B2(IA[5]), .A3(U298_qa[4]), .B3(IA[4]), .A4(INDEX_L), .B4(IA[11]),
    .A1(U170A_out));
  nand U275A (U275A_out, U120_y1, U125_q7);
  nand U430 (LOADC_L, U240_q4[7], U240_q4[5], U240_q4[3], GTMODE_L, G0, U240_q3[2], U240_q3[4], U240_q3[6]);
  not U100B (U100B_out, CLK_4_8_MHz);
  not U495C (CLK_2_4_MHz_L, CLK_2_4_MHz_t);
  not U410F (CLK_2_4_MHz, CLK_2_4_MHz_t);
  nand U205B (U205B_out, U408_y13, U408_y14);
  nand U205C (U205C_out, U408_y23, U408_y24);
  ttl_74670 U195 (
    .Q1(U195_q1), .Q2(U195_q2), .Q3(U195_q3), .Q4(U195_q4), .RA(GTMODE), .RB(CLK_2_4_MHz_t), .GR(1'b0),
    .D2(ID[5]), .D3(ID[6]), .D4(ID[7]), .WA(IA[0]), .WB(IA[1]), .GW(HSEL_L), .D1(ID[4]));
  xor U310A (U310A_out, GTMODE, CLK_2_4_MHz_t);
  or U115D (U115D_out, U120_y2, U275A_out);
  and U108A (U108A_out, T1, U100A_out);
  not U100A (U100A_out, LOADC_L);
  xor U310D (U310D_out, VDRIVE_GREEN, U420_q2);
  xor U265B (CSYNC_CROM_L, U205B_out, 1'b1);
  nand U270C (U270C_out, R[3], R[6], R[7]);
  nand U275D (U275D_out, R[4], R[6]);
  or U115C (U115C_out, U120_y3, U115D_out);
  or U110C (U110C_out, U115C_out, HD);
  or U110F (U110F_out, U125_q4, U108A_out);
  nand U205D (IDP_LOCKOUT, LOADC_L, GTMODE_L);
  and U210C (U210C_out, Q_1, U560_qb0);
  ttl_74157 U160 (
    .Y1(U260_y4[9]), .Y2(U260_y4[8]), .Y3(U260_y4[7]), .Y4(U260_y4[6]), .STROBE(U170B_out), .SEL(U170D_out),
    .B1(IA[9]), .A2(U298_qa[8]), .B2(IA[8]), .A3(U298_qa[7]), .B3(IA[7]), .A4(U298_qa[6]), .B4(IA[6]),
    .A1(U298_qa[9]));
  xor U265A (U265A_out, 1'b1, U260_y4[11]);
  ttl_74273 U240 (
    .Q1(G0), .Q2(T1), .Q3(U240_q3[2]), .Q4(U240_q4[3]), .Q5(U240_q3[4]), .Q6(U240_q4[5]), .Q7(U240_q3[6]),
    .Q8(U240_q4[7]), .CLK(U310A_out), .CLR(1'b1), .D1(Y[0]), .D2(Y[1]), .D3(Y[2]), .D4(Y[3]), .D5(Y[4]),
    .D6(Y[5]), .D7(Y[6]), .D8(Y[7]));
  // NoConnect on undriven_7
  ttl_7474 U305B (.NQ(U305B_nq), .Q(U305B_q), .CLK(CLK_2_4_MHz_L), .R(1'b1), .S(U205C_out), .D(U405E_out));
  not U410C (U410C_out, U205C_out);
  ttl_74279_sr U480B (.Q(LATCH_200_L), .S(VRES_L), .R(U270C_out));
  not not_2 (not_2_out, U198_rco);
  ttl_74163 U198 (
    .QA(U298_qa[4]), .QB(U298_qa[5]), .QC(U198_qc), .QD(U198_qd), .RCO(U198_rco), .ENP(1'b1), .ENT(U298_rco),
    .CLR(not_1_out), .LD(nor_1_out), .CLK(CLK_2_4_MHz_t), .A(U195_q1), .B(U195_q2), .C(U195_q3), .D(U195_q4));
  // NoConnect on U198_qc
  // NoConnect on U198_qd
  // NoConnect on U560_qa0
  ttl_74393 U560 (
    .QA0(U560_qa0), .QA1(U560_qa1), .QA2(U560_qa2), .QA3(U560_qa3), .QB0(U560_qb0), .QB1(U560_qb1),
    .QB2(U560_qb2), .QB3(U560_qb3), .CLR_A(U210C_out), .CLK_A(CLK_2_4_MHz_t), .CLR_B(U210C_out),
    .CLK_B(U560_qa3));
  // NoConnect on U560_qa1
  // NoConnect on U560_qa2
  // NoConnect on U560_qb1
  // NoConnect on U560_qb3
  or U405D (IWAIT_L, U305B_nq, U410C_out);
  or U105B (LOE_L, U410C_out, RD_L);
  nor nor_1 (nor_1_out, ~LOADC_L, ~not_2_out);  // NOR_Gate
  ttl_74273 U125 (
    .Q1(U125_q1), .Q2(U125_q2), .Q3(U125_q3), .Q4(U125_q4), .Q5(U125_q5), .Q6(U125_q6), .Q7(U125_q7),
    .Q8(GTMODE), .CLK(CLK_2_4_MHz_t), .CLR(CB_L), .D1(GTMODE), .D2(U125_q1), .D3(undriven_7), .D4(U110F_out),
    .D5(BIT0), .D6(BIT1), .D7(U210A_out), .D8(IDP_LOCKOUT));
  // NoConnect on U125_q3
  ttl_7474 U305A (.NQ(U305A_nq), .Q(U305A_q), .CLK(U100B_out), .R(1'b1), .S(U205C_out), .D(U305B_q));
  mem_6116P_2 U245 (
    .OD0(Y[0]), .OD1(Y[1]), .OD2(Y[2]), .OD3(Y[3]), .OD4(Y[4]), .OD5(Y[5]), .OD6(Y[6]), .OD7(Y[7]),
    .A2(U260_y4[2]), .A3(U260_y4[3]), .A4(U260_y4[4]), .A5(U260_y4[5]), .A6(U260_y4[6]), .A7(U260_y4[7]),
    .A8(U260_y4[8]), .A9(U260_y4[9]), .A10(U260_y4[10]), .A0(U260_y4[0]), .A1(U260_y4[1]), .OE(OE_L),
    .CS(U265A_out), .WE(BUF_L), .ID0(Y[0]), .ID1(Y[1]), .ID2(Y[2]), .ID3(Y[3]), .ID4(Y[4]), .ID5(Y[5]),
    .ID6(Y[6]), .ID7(Y[7]));
  not U100F (TMODE_L, U125_q4);
  and U108D (U108D_out, U125_q4, VDRIVE_GREEN);
  and U210B (U210B_out, HDRIVE_L, U270A_out);
  ttl_7474 U435A (.NQ(U435A_nq), .Q(U435A_q), .CLK(CLK_2_4_MHz_L), .R(1'b1), .S(U495A_out), .D(U410E_out));
  // NoConnect on U435A_nq
  or U405B (LCP, U305A_nq, U305B_q);
  ttl_74279_ssr U480C (.Q(U480C_q), .S2(VRES_L), .R(U275D_out), .S1(LATCH_200_L));
  xor U265D (U265D_out, CLK_4_8_MHz, U125_q5);
  xor U265C (U265C_out, CLK_2_4_MHz_t, U125_q6);
  not U208D (U208D_out, U210B_out);
  or U110A (U110A_out, LCP, IWR_L);
  pal_3358 U230 (
    .B1(U230_b1), .B2(U230_b2), .B3(U230_b3), .B4(U125_q4), .B5(U230_b0[1]), .B6(U230_b0[2]),
    .B7(U230_b0[3]), .B0(U230_b0[0]), .I1(U240_q3[4]), .I2(U240_q4[3]), .I3(U240_q3[2]), .I4(T1), .I5(G0),
    .I6(U130_d0[3]), .I7(U130_d0[2]), .I8(U130_d0[1]), .I9(U130_d0[0]), .I0(U240_q4[5]));
  // NoConnect on U230_b1
  // NoConnect on U230_b2
  ttl_74273 U225 (
    .Q1(U225_q1), .Q2(U225_q2), .Q3(U225_q3), .Q4(U225_q4), .Q5(U225_q5), .Q6(U225_q6), .Q7(U225_q7),
    .Q8(U225_q8), .CLK(CLK_2_4_MHz_t), .CLR(U110C_out), .D1(U230_b0[0]), .D2(U230_b0[1]), .D3(U230_b0[2]),
    .D4(U230_b0[3]), .D5(U230_b0[4]), .D6(U230_b0[5]), .D7(U230_b0[6]), .D8(U230_b0[7]));
  and U270B (U270B_out, U265D_out, CLK_9_8_MHz, U265C_out);
  not U208A (GTMODE_L, GTMODE);
  and U210A (U210A_out, GTMODE, TMODE_L);
  or U405C (U405C_out, U435A_q, U310B_out);
  ttl_74670 U285 (
    .Q1(U285_q1), .Q2(U285_q2), .Q3(U285_q3), .Q4(U285_q4), .RA(U480A_q), .RB(U480C_q), .GR(1'b0),
    .D2(ID[1]), .D3(ID[2]), .D4(ID[3]), .WA(IA[0]), .WB(IA[1]), .GW(VSEL_L), .D1(ID[0]));
  mem_6116P_2 U145 (
    .OD0(Y[0]), .OD1(Y[1]), .OD2(Y[2]), .OD3(Y[3]), .OD4(Y[4]), .OD5(Y[5]), .OD6(Y[6]), .OD7(Y[7]),
    .A2(U260_y4[2]), .A3(U260_y4[3]), .A4(U260_y4[4]), .A5(U260_y4[5]), .A6(U260_y4[6]), .A7(U260_y4[7]),
    .A8(U260_y4[8]), .A9(U260_y4[9]), .A10(U260_y4[10]), .A0(U260_y4[0]), .A1(U260_y4[1]), .OE(OE_L),
    .CS(U260_y4[11]), .WE(BUF_L), .ID0(Y[0]), .ID1(Y[1]), .ID2(Y[2]), .ID3(Y[3]), .ID4(Y[4]), .ID5(Y[5]),
    .ID6(Y[6]), .ID7(Y[7]));
  or U115A (PRE_GT_BLNK_L, U125_q2, GTMODE_L);
  or U105C (U230_b3, U210A_out, U108D_out);
  ttl_7474 U200A (.NQ(U200A_nq), .Q(BUF_L), .CLK(CLK_4_8_MHz), .R(1'b1), .S(U305A_q), .D(U110A_out));
  // NoConnect on U200A_nq
  ttl_74279_ssr U480A (.Q(U480A_q), .S2(U275B_out), .R(VRES_L), .S1(LATCH_200_L));
  ttl_74166 ttl_74166_1 (
    .QH(ttl_74166_1_qh), .CLK(CLK_19_6_MHz), .CLK_INH(1'b0), .CLR(1'b1), .SH_LD(U270B_out), .SER(1'b0),
    .A(U225_q1), .B(U225_q2), .C(U225_q3), .D(U225_q4), .E(U225_q5), .F(U225_q6), .G(U225_q7), .H(U225_q8));
  ttl_74273 U220 (
    .Q1(HD), .Q2(CB), .Q3(T_1), .Q4(Q_1), .Q5(U220_q5), .Q6(G_0), .Q7(U220_q7), .Q8(CB_L),
    .CLK(CLK_2_4_MHz_L), .CLR(1'b1), .D1(Q_1), .D2(U208D_out), .D3(T1), .D4(U560_qb2), .D5(U270A_out),
    .D6(G0), .D7(PRE_GT_BLNK_L), .D8(U210B_out));
  ttl_74283 U290 (
    .E1(L[0]), .E2(L[1]), .E3(L[2]), .E4(U298_qa[6]), .C4(U290_c4), .A1(U285_q1), .A2(U285_q3), .A3(R[0]),
    .A4(R[2]), .B1(U285_q2), .B2(U285_q4), .B3(R[1]), .B4(R[3]), .C0(1'b0));
  or U405F (U405F_out, ttl_74166_1_qh, U405A_out);
  ttl_7474 U200B (.NQ(U200B_nq), .Q(OE_L), .CLK(CLK_9_8_MHz), .R(1'b1), .S(U110A_out), .D(1'b0));
  // NoConnect on U200B_nq
  // NoConnect on undriven_8
  D_Flip_Flop U415B (
    .D(U405F_out), .clk(CLK_19_6_MHz), .Q(U415B_q), .Qn(VIDEO), .preset(undriven_8), .reset(undriven_9));
  // NoConnect on U415B_q
  // NoConnect on undriven_9
  not U208C (HDRIVE_L, HD);
  not U208F (U208F_out, U220_q5);
  nand U108C (U108C_out, U220_q5, U270A_out);
  nand U275B (U275B_out, HD, U190_c4);
  ttl_74244_joined U255 (
    .Y1(Y[0]), .Y2(Y[1]), .Y3(Y[2]), .Y4(Y[3]), .Y5(Y[4]), .Y6(Y[5]), .Y7(Y[6]), .Y8(Y[7]), .A1(ID[0]),
    .A2(ID[1]), .A3(ID[2]), .A4(ID[3]), .A5(ID[4]), .A6(ID[5]), .A7(ID[6]), .A8(ID[7]), .G(BUF_L));
  pal_3358 U235 (
    .B1(U235_b1), .B2(U235_b2), .B3(U230_b3), .B4(U125_q4), .B5(U230_b0[5]), .B6(U230_b0[6]),
    .B7(U230_b0[7]), .B0(U230_b0[4]), .I1(G_0), .I2(U240_q4[7]), .I3(U240_q3[6]), .I4(U240_q4[5]),
    .I5(U240_q3[4]), .I6(U130_d0[7]), .I7(U130_d0[6]), .I8(U130_d0[5]), .I9(U130_d0[4]), .I0(T_1));
  // NoConnect on U235_b1
  // NoConnect on U235_b2
  ttl_74279_sr ttl_74279_sr_1 (.Q(ttl_74279_sr_1_q), .S(U108C_out), .R(U405C_out));
  // NoConnect on U308A_q
  ttl_7474 U308A (.NQ(GT_BLNK), .Q(U308A_q), .CLK(CLK_19_6_MHz), .R(U220_q7), .S(1'b1), .D(U220_q7));
  not U100C (U100C_out, GT_BLNK);
  ttl_74670 U185 (
    .Q1(U185_q1), .Q2(U185_q2), .Q3(U185_q3), .Q4(U185_q4), .RA(U480A_q), .RB(U480C_q), .GR(1'b0),
    .D2(ID[5]), .D3(ID[6]), .D4(ID[7]), .WA(IA[0]), .WB(IA[1]), .GW(VSEL_L), .D1(ID[4]));
  or U105A (VLATCH, ttl_74279_sr_1_q, U310D_out);
  ttl_7474 U308B (.NQ(U308B_nq), .Q(CLK_9_8_MHz_L), .CLK(U100C_out), .R(1'b1), .S(1'b1), .D(U310C_out));
  rom_drom U175 (
    .D0(ID[0]), .D1(ID[1]), .D2(ID[2]), .D3(ID[3]), .D4(ID[4]), .D5(ID[5]), .D6(ID[6]), .D7(ID[7]),
    .OE(RD_L), .CE(DROM_L), .A1(IA[0]), .A2(IA[1]), .A3(IA[2]), .A4(IA[3]), .A5(IA[4]), .A6(IA[5]),
    .A7(IA[6]), .A8(IA[7]), .A9(IA[8]), .A10(IA[9]), .A11(IA[10]), .A12(IA[11]), .A13(IA[12]), .A14(1'b0),
    .A15(1'b1), .A16(1'b1));
  ttl_74374 U155 (
    .Q1(ID[0]), .Q2(ID[1]), .Q3(ID[2]), .Q4(ID[3]), .Q5(ID[4]), .Q6(ID[5]), .Q7(ID[6]), .Q8(ID[7]),
    .CLK(LCP), .OC(LOE_L), .D1(Y[0]), .D2(Y[1]), .D3(Y[2]), .D4(Y[3]), .D5(Y[4]), .D6(Y[5]), .D7(Y[6]),
    .D8(Y[7]));
  nand U275C (VRES_L, U208F_out, U270A_out);
  ttl_7474 U415A (.NQ(INDEX_L), .Q(VDRIVE_GREEN), .CLK(U208F_out), .R(1'b1), .S(1'b1), .D(INDEX_L));
  ttl_74283 U190 (
    .E1(U298_qa[7]), .E2(U298_qa[8]), .E3(U298_qa[9]), .E4(U298_qa[10]), .C4(U190_c4), .A1(U185_q1),
    .A2(U185_q3), .A3(R[4]), .A4(R[6]), .B1(U185_q2), .B2(U185_q4), .B3(R[5]), .B4(R[7]), .C0(U290_c4));
  xor U310B (U310B_out, U420_nq1, U308B_nq);
endmodule

module rom_char (
  input  OE,
  input  CE,
  input  A0,
  input  A1,
  input  A2,
  input  A3,
  input  A4,
  input  A5,
  input  A6,
  input  A7,
  input  A8,
  input  A9,
  input  A10,
  input  A11,
  output D0,
  output D1,
  output D2,
  output D3,
  output D4,
  output D5,
  output D6,
  output D7
);

  wire and_1_out;
  wire [7:0] rom_1_data;

  ROM #(.addrWidth(12)) rom_1 (.addr({A11, A10, A9, A8, A7, A6, A5, A4, A3, A2, A1, A0}), .data(rom_1_data));
  and and_1 (and_1_out, ~OE, ~CE);  // AND_Gate
  assign {D7, D6, D5, D4, D3, D2, D1, D0} = and_1_out ? rom_1_data : 8'bz;  // Controlled_Buffer controlled_buffer_1

  // Notes on the sheet:
  //   contents of rom_1 (hex, n*v repeats v):
  //   0 38 44 4c 54 64 44 38 0 10 30 50 10 10 10 7c 0 38 44 4 18 20 40 7c 0 38 44 4 18 4 44 38 0 8 18 28
  //   48 7c 8 8 0 7c 40 78 4 4 4 78 0 38 40 40 78 44 44 38 0 7c 4 8 4*10 0 38 44 44 38 44 44 38 0 38 44 44
  //   3c 4 4 38 0 10 28 44 44 7c 44 44 0 f8 44 44 78 44 44 f8 0 38 44 40 40 40 44 38 0 78 5*44 78 0 7c 40
  //   40 70 40 40 7c 0 7c 40 40 70 40 40 40 0 38 44 40 40 4c 44 3c 0 44 44 44 7c 44 44 44 0 38 5*10 38 0
  //   5*4 44 38 0 44 48 50 60 50 48 44 0 6*40 7c 0 44 6c 54 54 44 44 44 0 44 44 64 54 4c 44 44 0 38 5*44
  //   38 0 78 44 44 78 40 40 40 0 38 44 44 44 54 48 34 0 78 44 44 78 50 48 44 0 38 44 40 38 4 44 38 0 7c
  //   6*10 0 6*44 38 0 5*44 28 10 0 44 44 44 54 54 6c 44 0 44 44 28 10 28 44 44 0 44 44 28 4*10 0 7c 4 8
  //   10 20 40 7c 14*0 30 30 5*0 10 10 20 0 2 4 8 10 20 40 80 0 0 30 30 0 30 30 0 0 10 28 44 5*0 10 3c 50
  //   38 14 78 10 26*0 ee 28 10 28 ee 0 0 10 0 10 20 40 44 38 0 0 10 10 7c 10 10 5*0 7c 4*0 38 5*8 38 0 38
  //   5*20 38 0 10 54 38 fe 38 54 10 0 10 38 7c fe 7c 38 10 8*38 0 8 18 38 78 38 18 8 0 20 30 38 3c 38 30
  //   20 0 0 0 18 18 15*0 ff 7*0 66 5*0 e 8 10 20 e0 0 0 0 e0 20 10 8 e 0 80 40 20 10 8 4 2 1 0 5*10 0 10
  //   0 0 28 7c 28 7c 28 0 0 64 64 8 10 20 4c 4c 0 30 48 28 10 2a 44 3a 0 10 10 6*0 8 10 20 20 20 10 8 0
  //   20 10 8 8 8 10 20 0 0 0 7c 0 7c 0 0 0 80 40 20 10 8 4 2 15*0 7c 0 0 10 28 44 fe 4*0 48 48 48 74 80 0
  //   0 8 10 20 40 20 10 8 0 20 10 8 4 8 10 20 0 0 30 30 0 10 10 20 0 38 44 4 8 10 0 10 0 0 78 84 b4 b8 80
  //   78 0 10 3c 50 50 50 3c 10 4*0 7c 4 0 0 0 10 10 10 0 10 10 10 0 0 5*10 0 0 10 10 8 5*0 c 10 10 60 10
  //   10 c 0 60 10 10 c 10 10 60 0 0 0 60 92 c 0 0 0 1c 14 10 10 10 50 70 0 44 44 44 7c 10 10 10 0 4 4 4
  //   7c 44 44 44 0 7*10 0 6*80 0 0 6*c0 0 40 28 14 2a 15 a 5 a 1 a 14 2a 54 a8 50 a8 5 2 5 2 1 0 0 0 50
  //   a0 50 a0 40 80 5*0 ff ff 6*38 ff ff 0 0 0 38 38 38 3f 3f 6*38 f8 f8 6*38 ff ff 38 38 38 6*0 44 7c 0
  //   6*e0 0 0 6*f0 0 0 6*f8 0 0 6*fc 0 0 6*fe 0 0 6*ff 0 0 28 28 5*0 ff 6*0 10*ff 0 7c 10 10 10 0 ff 0 0
  //   0 ff ff 6*0 3f 3f 6*38 3f 3f 6*0 f8 f8 6*38 f8 f8 6*0 1 2 5 2 5 0 0 80 40 a0 50 a0 50 a 5 a 15 2a 14
  //   28 40 a8 50 a8 54 2a 14 a 1 8*0 ff 6*81 ff 8*0 ff c7 bb b3 ab 9b bb c7 ff ef cf af ef ef ef 83 ff c7
  //   bb fb e7 df bf 83 ff c7 bb fb e7 fb bb c7 ff f7 e7 d7 b7 83 f7 f7 ff 83 bf 87 fb fb fb 87 ff c7 bf
  //   bf 87 bb bb c7 ff 83 fb f7 4*ef ff c7 bb bb c7 bb bb c7 ff c7 bb bb c3 fb fb c7 ff ef d7 bb bb 83 bb
  //   bb ff 7 bb bb 87 bb bb 7 ff c7 bb bf bf bf bb c7 ff 87 5*bb 87 ff 83 bf bf 8f bf bf 83 ff 83 bf bf
  //   8f bf bf bf ff c7 bb bf bf b3 bb c3 ff bb bb bb 83 bb bb bb ff c7 5*ef c7 ff 5*fb bb c7 ff bb b7 af
  //   9f af b7 bb ff 6*bf 83 ff bb 93 ab ab bb bb bb ff bb bb 9b ab b3 bb bb ff c7 5*bb c7 ff 87 bb bb 87
  //   bf bf bf ff c7 bb bb bb ab b7 cb ff 87 bb bb 87 af b7 bb ff c7 bb bf c7 fb bb c7 ff 83 6*ef ff 6*bb
  //   c7 ff 5*bb d7 ef ff bb bb bb ab ab 93 bb ff bb bb d7 ef d7 bb bb ff bb bb d7 4*ef ff 83 fb f7 ef df
  //   bf 83 14*ff cf cf 5*ff ef ef df ff fd fb f7 ef df bf 7f ff ff cf cf ff cf cf ff ff ef d7 bb 5*ff ef
  //   c3 af c7 eb 87 ef 26*ff 11 d7 ef d7 11 ff ff ef ff ef df bf bb c7 ff ff ef ef 83 ef ef 5*ff 83 4*ff
  //   c7 5*f7 c7 ff c7 5*df c7 ff ef ab c7 1 c7 ab ef ff ef c7 83 1 83 c7 ef 8*c7 ff f7 e7 c7 87 c7 e7 f7
  //   ff df cf c7 c3 c7 cf df ff ff ff e7 e7 15*ff 0 7*ff 99 5*ff f1 f7 ef df 1f ff ff ff 1f df ef f7 f1
  //   ff 7f bf df ef f7 fb fd fe ff 5*ef ff ef ff ff d7 83 d7 83 d7 ff ff 9b 9b f7 ef df b3 b3 ff cf b7 d7
  //   ef d5 bb c5 ff ef ef 6*ff f7 ef df df df ef f7 ff df ef f7 f7 f7 ef df ff ff ff 83 ff 83 ff ff ff 7f
  //   bf df ef f7 fb fd 15*ff 83 ff ff ef d7 bb 1 4*ff b7 b7 b7 8b 7f ff ff f7 ef df bf df ef f7 ff df ef
  //   f7 fb f7 ef df ff ff cf cf ff ef ef df ff c7 bb fb f7 ef ff ef ff ff 87 7b 4b 47 7f 87 ff ef c3 af
  //   af af c3 ef 4*ff 83 fb ff ff ff ef ef ef ff ef ef ef ff ff 5*ef ff ff ef ef f7 5*ff f3 ef ef 9f ef
  //   ef f3 ff 9f ef ef f3 ef ef 9f ff ff ff 9f 6d f3 ff ff ff e3 eb ef ef ef af 8f ff bb bb bb 83 ef ef
  //   ef ff fb fb fb 83 bb bb bb ff 7*ef ff 6*7f ff ff 6*3f ff bf d7 eb d5 ea f5 fa f5 fe f5 eb d5 ab 57
  //   af 57 fa fd fa fd fe ff ff ff af 5f af 5f bf 7f 5*ff 0 0 6*c7 0 0 ff ff ff c7 c7 c7 c0 c0 6*c7 7 7
  //   6*c7 0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
endmodule

module rom_drom (
  input  OE,
  input  CE,
  input  A1,
  input  A2,
  input  A3,
  input  A4,
  input  A5,
  input  A6,
  input  A7,
  input  A8,
  input  A9,
  input  A10,
  input  A11,
  input  A12,
  input  A13,
  input  A14,
  input  A15,
  input  A16,
  output D0,
  output D1,
  output D2,
  output D3,
  output D4,
  output D5,
  output D6,
  output D7
);

  wire and_1_out;
  wire [7:0] rom_1_data;

  and and_1 (and_1_out, ~OE, ~CE);  // AND_Gate
  ROM #(.addrWidth(16)) rom_1 (
    .addr({A16, A15, A14, A13, A12, A11, A10, A9, A8, A7, A6, A5, A4, A3, A2, A1}), .data(rom_1_data));
  assign {D7, D6, D5, D4, D3, D2, D1, D0} = and_1_out ? rom_1_data : 8'bz;  // Controlled_Buffer controlled_buffer_1

  // Notes on the sheet:
  //   contents of rom_1 (hex, n*v repeats v):
  //   0 d 12 a 10 17 18 1c 1d 12 c 1c 24 12 17 24 19 1b 18 10 1b e 1c 1c 3e 0 32 0 ac 3e 1 32 80 a9 1 ff f
  //   21 0 d0 11 1 d0 3e 24 77 ed b0 21 0 c0 6 4 3e 0 77 23 10 fc 11 0 8 19 6 4 77 2b 10 fc 1 17 0 21 1 e0
  //   11 56 d3 ed b0 3e 2 32 80 a9 31 15 e1 11 b e1 c3 61 e0 cd 35 27 dd 21 0 0 dd 19 dd 4e 4 d9 dd 6e 6
  //   dd 66 7 dd 5e 6 dd 56 7 dd 46 9 dd 4e 8 3e aa 13 77 ed b0 13 7a dd 6e 6 dd 66 7 dd 5e 8 dd 56 9 8 3e
  //   aa 4e b9 c2 e7 e0 3e cc 77 23 8 47 8 78 bc c2 92 e0 dd 6e 6 dd 66 7 3e cc 4e b9 c2 e7 e0 3e f0 77 23
  //   8 47 8 78 bc c2 ab e0 dd 6e 6 dd 66 7 3e f0 4e b9 c2 e7 e0 3e f 77 23 8 47 8 78 bc c2 c4 e0 13 3e f
  //   2b 4e b9 47 c2 e7 e0 1b 7a b3 c2 d8 e0 8 d9 79 e6 3 fe 0 ca d e1 8 d9 78 6 1 dd 21 0 bc dd 70 1c dd
  //   77 1d dd 74 20 dd 75 1f dd 71 1e d9 cd 3c 27 8 c9 0 0 0 b0 ff f 17 e1 c2 34 e1 31 ff bf c3 a 2 ff f
  //   a 12 15 1e 1b e 5*24 12 18 19 24 1b a 16 1 c 0 21 21 e1 11 62 d3 ed b0 1 7 0 21 2d e1 11 50 d4 ed b0
  //   d9 8 7c 4*7 e6 f 32 62 d4 7c e6 f 32 63 d4 7d 4*7 e6 f 32 64 d4 7d e6 f 32 65 d4 8 4f 4*7 e6 f 32 67
  //   d4 79 e6 f 32 68 d4 7e 4*7 e6 f 32 6a d4 7e e6 f 32 6b d4 8 7c fe b8 da 97 e1 c3 9c e1 6 2 c3 9f e1
  //   6 3 af 11 ff 3f a8 32 80 a9 8 77 1b 4e 8 ba c2 a6 e1 c3 9f e1 cd 35 27 dd 21 0 0 dd 19 d9 11 1b bc
  //   21 1b bc 7a de c 57 ed a0 ed a0 ed a0 ed a0 ed a0 ed a0 dd 6e 4 dd 66 5 dd 4e 6 dd 46 7 dd 5e 8 dd
  //   56 9 ed b0 d9 dd 7e 5 fe bc c2 fb e1 7a de c 57 eb 23 77 2b eb c3 4 e2 7a c6 c 57 eb 23 77 2b eb c3
  //   3c 27 cd 41 27 21 4 0 19 7e fe 1 3e 4 20 1 f 32 a1 be cd bf b 21 1 0 e5 cd 62 10 f1 cd e5 1 af 32 a0
  //   be 21 a1 be 96 f2 72 e2 21 1 0 e5 cd 62 10 f1 79 32 a2 be cd e5 1 3a a2 be b7 28 18 3a a0 be 6f 26 0
  //   1 6c bc 9 3a 0 aa 77 21 4 0 cd 9d 27 cd 4b e4 f1 21 4 0 cd 9d 27 cd 4b e4 f1 3a a0 be 3c 32 a0 be 18
  //   b9 3a a2 be 4f c3 58 27 cd 41 27 3e 8 32 9e be cd bf b 21 1 0 e5 cd 62 10 f1 cd e5 1 af 32 9d be 21
  //   9e be 96 f2 d0 e2 21 1 0 e5 cd 62 10 f1 79 32 9f be cd e5 1 3a 9f be b7 28 e 3a 9d be 6f 26 0 1 6c
  //   bc 9 3a 0 aa 77 21 4 0 cd 9d 27 cd 4b e4 f1 3a 9d be 3c 32 9d be 18 c3 3a 9f be 4f c3 58 27 cd 41 27
  //   af 32 9b be 21 4 0 19 3a 9b be 96 f2 31 e3 21 3f d6 22 1f bc 21 6 0 19 7e 23 66 6f 7e 32 1d bc 2a 9b
  //   be 26 0 1 6c bc 9 7e 32 1e bc 3a 1c bc 3c 32 1c bc 21 6 0 cd 9d 27 21 6 0 19 34 30 2 23 34 2a 9b be
  //   26 0 1 6c bc 9 c1 a be 28 a e 0 c3 58 27 e f c3 58 27 3a 9b be 3c 32 9b be 18 9f cd 35 27 21 4 0 19
  //   7e 23 66 6f 22 1f bc 3e 0 32 1d bc 3e 1 32 1c bc 3a 36 bc e6 f 32 36 bc 3a 36 bc f6 80 32 36 bc 3a
  //   36 bc 32 0 a8 21 2 0 e5 cd 62 10 f1 79 32 7f be cd e5 1 3a 36 bc f6 1c 32 36 bc 3a 7f be b7 20 9 3a
  //   36 bc 32 0 a8 c3 3c 27 21 4 0 19 7e 23 66 6f 7e 32 1e bc 3a 1e bc b7 28 3 c3 3c 27 3e ff 32 1d bc 3e
  //   2 32 1c bc 3a 36 bc e6 f7 32 36 bc 3a 36 bc 32 0 a8 21 2 0 e5 cd 62 10 f1 79 32 7f be cd e5 1 3a 36
  //   bc f6 1c 32 36 bc 3a 7f be b7 20 9 3a 36 bc 32 0 a8 c3 3c 27 21 4 0 19 7e 23 66 6f 7e 32 1e bc 21 1d
  //   bc 3a 1e bc be 28 3 c3 3c 27 3e 3 32 1c bc 3e 0 32 1d bc 3a 36 bc e6 e7 32 36 bc 3a 36 bc 32 0 a8 21
  //   2 0 e5 cd 62 10 f1 79 32 7f be cd e5 1 3a 36 bc f6 1c 32 36 bc 3a 7f be b7 20 3 c3 3c 27 21 4 0 19
  //   7e 23 66 6f 7e 32 1e bc 3a 36 bc 32 0 a8 c3 3c 27 cd 35 27 21 4 0 19 7e b7 20 16 3a 77 bc 3c 32 77
  //   bc 32 0 c8 3a 76 bc 3c 32 76 bc 32 1 c8 18 a 3a 79 bc 3c 32 79 bc 32 3 c0 c3 3c 27 cd 35 27 3e 30 32
  //   77 bc 3e b0 32 76 bc 3e 8 32 1 c8 3e 90 32 2 c8 3e 0 32 2 c0 3e 0 32 3 c0 3e 0 32 0 c8 21 0 0 e5 cd
  //   4b e4 f1 c3 3c 27 854*ff cd f1 5e 3e 1 32 f6 b4 3e 1b 32 f7 b4 87 9f 32 f8 b4 21 f1 bc 22 f9 b4 21
  //   d6 bc 22 fb b4 21 f6 b4 e5 cd ac f2 f1 2a bf b5 7e fe 27 20 b 3a ca b6 32 23 bd cd 81 e8 18 17 21 4
  //   0 3a ca b6 4f 87 9f 47 7d 91 6f 7c 98 67 7d 32 23 bd cd a5 e9 2a c6 b4 e5 21 d6 bc c1 79 96 4f 78 23
  //   9e 47 79 32 c bd 1 1 0 c3 f8 5e 31 e9 14 0 31 e9 a 0 31 e9 5 0 b0 e8 2 0 91 e8 1 0 0 0 31 e9 cd f1
  //   5e 3a d4 bc 4f 87 9f 47 21 69 e8 c3 31 8f 2a cf bc 3a ca b6 4f 87 9f 47 7d 91 6f 7c 98 67 1 ff ff 9
  //   22 c6 b4 3e 1 32 d bd c3 f8 5e 3a ca b6 4f 87 9f 47 c5 3a d3 bc 4f 87 9f 47 e1 7d 91 6f 7c 98 67 3e
  //   1 95 3e 0 9c f2 db e8 2a cf bc 1 fe ff 9 22 c6 b4 18 1c 21 d3 bc 3a ca b6 be f2 ed e8 2a cf b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
endmodule

module pal_3358 (
  input  I0,
  input  I1,
  input  I2,
  input  I3,
  input  I4,
  input  I5,
  input  I6,
  input  I7,
  input  I8,
  input  I9,
  output B0,
  output B1,
  output B2,
  output B3,
  output B4,
  output B5,
  output B6,
  output B7
);

  PLA #(.in_width(10), .out_width(8), .\table ("0000000000 11010111\n0000000001 11010111\n0000000010 11010111\n0000000011 11010111\n0000000100 11010111\n0000000101 11010111\n0000000110 11010111\n0000000111 11010111\n0000001000 11010111\n0000001001 11010111\n0000001010 11010111\n0000001011 11010111\n0000001100 11010111\n0000001101 11010111\n0000001110 11010111\n0000001111 11010111\n0000010000 11010111\n0000010001 11010111\n0000010010 11010111\n0000010011 11010111\n0000010100 11010111\n0000010101 11010111\n0000010110 11010111\n0000010111 11010111\n0000011000 11010111\n0000011001 11010111\n0000011010 11010111\n0000011011 11010111\n0000011100 11010111\n0000011101 11010111\n0000011110 11010111\n0000011111 11010111\n0000100000 11000111\n0000100001 11000111\n0000100010 11000111\n0000100011 11000111\n0000100100 11000111\n0000100101 11000111\n0000100110 11000111\n0000100111 11000111\n0000101000 11000111\n0000101001 11000111\n0000101010 11000111\n0000101011 11000111\n0000101100 11000111\n0000101101 11000111\n0000101110 11000111\n0000101111 11000111\n0000110000 11000111\n0000110001 11000111\n0000110010 11000111\n0000110011 11000111\n0000110100 11000111\n0000110101 11000111\n0000110110 11000111\n0000110111 11000111\n0000111000 11000111\n0000111001 11000111\n0000111010 11000111\n0000111011 11000111\n0000111100 11000111\n0000111101 11000111\n0000111110 11000111\n0000111111 11000111\n0001000000 11010111\n0001000001 11010111\n0001000010 11010111\n0001000011 11010111\n0001000100 11010111\n0001000101 11010111\n0001000110 11010111\n0001000111 11010111\n0001001000 11010111\n0001001001 11010111\n0001001010 11010111\n0001001011 11010111\n0001001100 11010111\n0001001101 11010111\n0001001110 11010111\n0001001111 11010111\n0001010000 11010111\n0001010001 11010111\n0001010010 11010111\n0001010011 11010111\n0001010100 11010111\n0001010101 11010111\n0001010110 11010111\n0001010111 11010111\n0001011000 11010111\n0001011001 11010111\n0001011010 11010111\n0001011011 11010111\n0001011100 11010111\n0001011101 11010111\n0001011110 11010111\n0001011111 11010111\n0001100000 11000111\n0001100001 11000111\n0001100010 11000111\n0001100011 11000111\n0001100100 11000111\n0001100101 11000111\n0001100110 11000111\n0001100111 11000111\n0001101000 11000111\n0001101001 11000111\n0001101010 11000111\n0001101011 11000111\n0001101100 11000111\n0001101101 11000111\n0001101110 11000111\n0001101111 11000111\n0001110000 11000111\n0001110001 11000111\n0001110010 11000111\n0001110011 11000111\n0001110100 11000111\n0001110101 11000111\n0001110110 11000111\n0001110111 11000111\n0001111000 11000111\n0001111001 11000111\n0001111010 11000111\n0001111011 11000111\n0001111100 11000111\n0001111101 11000111\n0001111110 11000111\n0001111111 11000111\n0010000000 11010111\n0010000001 11010111\n0010000010 11010111\n0010000011 11010111\n0010000100 11010111\n0010000101 11010111\n0010000110 11010111\n0010000111 11010111\n0010001000 11010111\n0010001001 11010111\n0010001010 11010111\n0010001011 11010111\n0010001100 11010111\n0010001101 11010111\n0010001110 11010111\n0010001111 11010111\n0010010000 11010111\n0010010001 11010111\n0010010010 11010111\n0010010011 11010111\n0010010100 11010111\n0010010101 11010111\n0010010110 11010111\n0010010111 11010111\n0010011000 11010111\n0010011001 11010111\n0010011010 11010111\n0010011011 11010111\n0010011100 11010111\n0010011101 11010111\n0010011110 11010111\n0010011111 11010111\n0010100000 11000111\n0010100001 11000111\n0010100010 11000111\n0010100011 11000111\n0010100100 11000111\n0010100101 11000111\n0010100110 11000111\n0010100111 11000111\n0010101000 11000111\n0010101001 11000111\n0010101010 11000111\n0010101011 11000111\n0010101100 11000111\n0010101101 11000111\n0010101110 11000111\n0010101111 11000111\n0010110000 11000111\n0010110001 11000111\n0010110010 11000111\n0010110011 11000111\n0010110100 11000111\n0010110101 11000111\n0010110110 11000111\n0010110111 11000111\n0010111000 11000111\n0010111001 11000111\n0010111010 11000111\n0010111011 11000111\n0010111100 11000111\n0010111101 11000111\n0010111110 11000111\n0010111111 11000111\n0011000000 11010111\n0011000001 11010111\n0011000010 11010111\n0011000011 11010111\n0011000100 11010111\n0011000101 11010111\n0011000110 11010111\n0011000111 11010111\n0011001000 11010111\n0011001001 11010111\n0011001010 11010111\n0011001011 11010111\n0011001100 11010111\n0011001101 11010111\n0011001110 11010111\n0011001111 11010111\n0011010000 11010111\n0011010001 11010111\n0011010010 11010111\n0011010011 11010111\n0011010100 11010111\n0011010101 11010111\n0011010110 11010111\n0011010111 11010111\n0011011000 11010111\n0011011001 11010111\n0011011010 11010111\n0011011011 11010111\n0011011100 11010111\n0011011101 11010111\n0011011110 11010111\n0011011111 11010111\n0011100000 11000111\n0011100001 11000111\n0011100010 11000111\n0011100011 11000111\n0011100100 11000111\n0011100101 11000111\n0011100110 11000111\n0011100111 11000111\n0011101000 11000111\n0011101001 11000111\n0011101010 11000111\n0011101011 11000111\n0011101100 11000111\n0011101101 11000111\n0011101110 11000111\n0011101111 11000111\n0011110000 11000111\n0011110001 11000111\n0011110010 11000111\n0011110011 11000111\n0011110100 11000111\n0011110101 11000111\n0011110110 11000111\n0011110111 11000111\n0011111000 11000111\n0011111001 11000111\n0011111010 11000111\n0011111011 11000111\n0011111100 11000111\n0011111101 11000111\n0011111110 11000111\n0011111111 11000111\n0100000000 11010111\n0100000001 11010111\n0100000010 11010111\n0100000011 11010111\n0100000100 11010111\n0100000101 11010111\n0100000110 11010111\n0100000111 11010111\n0100001000 11010111\n0100001001 11010111\n0100001010 11010111\n0100001011 11010111\n0100001100 11010111\n0100001101 11010111\n0100001110 11010111\n0100001111 11010111\n0100010000 11010111\n0100010001 11010111\n0100010010 11010111\n0100010011 11010111\n0100010100 11010111\n0100010101 11010111\n0100010110 11010111\n0100010111 11010111\n0100011000 11010111\n0100011001 11010111\n0100011010 11010111\n0100011011 11010111\n0100011100 11010111\n0100011101 11010111\n0100011110 11010111\n0100011111 11010111\n0100100000 11000111\n0100100001 11000111\n0100100010 11000111\n0100100011 11000111\n0100100100 11000111\n0100100101 11000111\n0100100110 11000111\n0100100111 11000111\n0100101000 11000111\n0100101001 11000111\n0100101010 11000111\n0100101011 11000111\n0100101100 11000111\n0100101101 11000111\n0100101110 11000111\n0100101111 11000111\n0100110000 11000111\n0100110001 11000111\n0100110010 11000111\n0100110011 11000111\n0100110100 11000111\n0100110101 11000111\n0100110110 11000111\n0100110111 11000111\n0100111000 11000111\n0100111001 11000111\n0100111010 11000111\n0100111011 11000111\n0100111100 11000111\n0100111101 11000111\n0100111110 11000111\n0100111111 11000111\n0101000000 11010111\n0101000001 11010111\n0101000010 11010111\n0101000011 11010111\n0101000100 11010111\n0101000101 11010111\n0101000110 11010111\n0101000111 11010111\n0101001000 11010111\n0101001001 11010111\n0101001010 11010111\n0101001011 11010111\n0101001100 11010111\n0101001101 11010111\n0101001110 11010111\n0101001111 11010111\n0101010000 11010111\n0101010001 11010111\n0101010010 11010111\n0101010011 11010111\n0101010100 11010111\n0101010101 11010111\n0101010110 11010111\n0101010111 11010111\n0101011000 11010111\n0101011001 11010111\n0101011010 11010111\n0101011011 11010111\n0101011100 11010111\n0101011101 11010111\n0101011110 11010111\n0101011111 11010111\n0101100000 11000111\n0101100001 11000111\n0101100010 11000111\n0101100011 11000111\n0101100100 11000111\n0101100101 11000111\n0101100110 11000111\n0101100111 11000111\n0101101000 11000111\n0101101001 11000111\n0101101010 11000111\n0101101011 11000111\n0101101100 11000111\n0101101101 11000111\n0101101110 11000111\n0101101111 11000111\n0101110000 11000111\n0101110001 11000111\n0101110010 11000111\n0101110011 11000111\n0101110100 11000111\n0101110101 11000111\n0101110110 11000111\n0101110111 11000111\n0101111000 11000111\n0101111001 11000111\n0101111010 11000111\n0101111011 11000111\n0101111100 11000111\n0101111101 11000111\n0101111110 11000111\n0101111111 11000111\n0110000000 11010111\n0110000001 11010111\n0110000010 11010111\n0110000011 11010111\n0110000100 11010111\n0110000101 11010111\n0110000110 11010111\n0110000111 11010111\n0110001000 11010111\n0110001001 11010111\n0110001010 11010111\n0110001011 11010111\n0110001100 11010111\n0110001101 11010111\n0110001110 11010111\n0110001111 11010111\n0110010000 11010111\n0110010001 11010111\n0110010010 11010111\n0110010011 11010111\n0110010100 11010111\n0110010101 11010111\n0110010110 11010111\n0110010111 11010111\n0110011000 11010111\n0110011001 11010111\n0110011010 11010111\n0110011011 11010111\n0110011100 11010111\n0110011101 11010111\n0110011110 11010111\n0110011111 11010111\n0110100000 11000111\n0110100001 11000111\n0110100010 11000111\n0110100011 11000111\n0110100100 11000111\n0110100101 11000111\n0110100110 11000111\n0110100111 11000111\n0110101000 11000111\n0110101001 11000111\n0110101010 11000111\n0110101011 11000111\n0110101100 11000111\n0110101101 11000111\n0110101110 11000111\n0110101111 11000111\n0110110000 11000111\n0110110001 11000111\n0110110010 11000111\n0110110011 11000111\n0110110100 11000111\n0110110101 11000111\n0110110110 11000111\n0110110111 11000111\n0110111000 11000111\n0110111001 11000111\n0110111010 11000111\n0110111011 11000111\n0110111100 11000111\n0110111101 11000111\n0110111110 11000111\n0110111111 11000111\n0111000000 11010111\n0111000001 11010111\n0111000010 11010111\n0111000011 11010111\n0111000100 11010111\n0111000101 11010111\n0111000110 11010111\n0111000111 11010111\n0111001000 11010111\n0111001001 11010111\n0111001010 11010111\n0111001011 11010111\n0111001100 11010111\n0111001101 11010111\n0111001110 11010111\n0111001111 11010111\n0111010000 11010111\n0111010001 11010111\n0111010010 11010111\n0111010011 11010111\n0111010100 11010111\n0111010101 11010111\n0111010110 11010111\n0111010111 11010111\n0111011000 11010111\n0111011001 11010111\n0111011010 11010111\n0111011011 11010111\n0111011100 11010111\n0111011101 11010111\n0111011110 11010111\n0111011111 11010111\n0111100000 11000111\n0111100001 11000111\n0111100010 11000111\n0111100011 11000111\n0111100100 11000111\n0111100101 11000111\n0111100110 11000111\n0111100111 11000111\n0111101000 11000111\n0111101001 11000111\n0111101010 11000111\n0111101011 11000111\n0111101100 11000111\n0111101101 11000111\n0111101110 11000111\n0111101111 11000111\n0111110000 11000111\n0111110001 11000111\n0111110010 11000111\n0111110011 11000111\n0111110100 11000111\n0111110101 11000111\n0111110110 11000111\n0111110111 11000111\n0111111000 11000111\n0111111001 11000111\n0111111010 11000111\n0111111011 11000111\n0111111100 11000111\n0111111101 11000111\n0111111110 11000111\n0111111111 11000111\n1000000000 11010111\n1000000001 11010111\n1000000010 11010111\n1000000011 11010111\n1000000100 11010111\n1000000101 11010111\n1000000110 11010111\n1000000111 11010111\n1000001000 11010111\n1000001001 11010111\n1000001010 11010111\n1000001011 11010111\n1000001100 11010111\n1000001101 11010111\n1000001110 11010111\n1000001111 11010111\n1000010000 11010111\n1000010001 11010111\n1000010010 11010111\n1000010011 11010111\n1000010100 11010111\n1000010101 11010111\n1000010110 11010111\n1000010111 11010111\n1000011000 11010111\n1000011001 11010111\n1000011010 11010111\n1000011011 11010111\n1000011100 11010111\n1000011101 11010111\n1000011110 11010111\n1000011111 11010111\n1000100000 11000111\n1000100001 11000111\n1000100010 11000111\n1000100011 11000111\n1000100100 11000111\n1000100101 11000111\n1000100110 11000111\n1000100111 11000111\n1000101000 11000111\n1000101001 11000111\n1000101010 11000111\n1000101011 11000111\n1000101100 11000111\n1000101101 11000111\n1000101110 11000111\n1000101111 11000111\n1000110000 11000111\n1000110001 11000111\n1000110010 11000111\n1000110011 11000111\n1000110100 11000111\n1000110101 11000111\n1000110110 11000111\n1000110111 11000111\n1000111000 11000111\n1000111001 11000111\n1000111010 11000111\n1000111011 11000111\n1000111100 11000111\n1000111101 11000111\n1000111110 11000111\n1000111111 11000111\n1001000000 11010111\n1001000001 11010111\n1001000010 11010111\n1001000011 11010111\n1001000100 11010111\n1001000101 11010111\n1001000110 11010111\n1001000111 11010111\n1001001000 11010111\n1001001001 11010111\n1001001010 11010111\n1001001011 11010111\n1001001100 11010111\n1001001101 11010111\n1001001110 11010111\n1001001111 11010111\n1001010000 11010111\n1001010001 11010111\n1001010010 11010111\n1001010011 11010111\n1001010100 11010111\n1001010101 11010111\n1001010110 11010111\n1001010111 11010111\n1001011000 11010111\n1001011001 11010111\n1001011010 11010111\n1001011011 11010111\n1001011100 11010111\n1001011101 11010111\n1001011110 11010111\n1001011111 11010111\n1001100000 11000111\n1001100001 11000111\n1001100010 11000111\n1001100011 11000111\n1001100100 11000111\n1001100101 11000111\n1001100110 11000111\n1001100111 11000111\n1001101000 11000111\n1001101001 11000111\n1001101010 11000111\n1001101011 11000111\n1001101100 11000111\n1001101101 11000111\n1001101110 11000111\n1001101111 11000111\n1001110000 11000111\n1001110001 11000111\n1001110010 11000111\n1001110011 11000111\n1001110100 11000111\n1001110101 11000111\n1001110110 11000111\n1001110111 11000111\n1001111000 11000111\n1001111001 11000111\n1001111010 11000111\n1001111011 11000111\n1001111100 11000111\n1001111101 11000111\n1001111110 11000111\n1001111111 11000111\n1010000000 11010111\n1010000001 11010111\n1010000010 11010111\n1010000011 11010111\n1010000100 11010111\n1010000101 11010111\n1010000110 11010111\n1010000111 11010111\n1010001000 11010111\n1010001001 11010111\n1010001010 11010111\n1010001011 11010111\n1010001100 11010111\n1010001101 11010111\n1010001110 11010111\n1010001111 11010111\n1010010000 11010111\n1010010001 11010111\n1010010010 11010111\n1010010011 11010111\n1010010100 11010111\n1010010101 11010111\n1010010110 11010111\n1010010111 11010111\n1010011000 11010111\n1010011001 11010111\n1010011010 11010111\n1010011011 11010111\n1010011100 11010111\n1010011101 11010111\n1010011110 11010111\n1010011111 11010111\n1010100000 11000111\n1010100001 11000111\n1010100010 11000111\n1010100011 11000111\n1010100100 11000111\n1010100101 11000111\n1010100110 11000111\n1010100111 11000111\n1010101000 11000111\n1010101001 11000111\n1010101010 11000111\n1010101011 11000111\n1010101100 11000111\n1010101101 11000111\n1010101110 11000111\n1010101111 11000111\n1010110000 11000111\n1010110001 11000111\n1010110010 11000111\n1010110011 11000111\n1010110100 11000111\n1010110101 11000111\n1010110110 11000111\n1010110111 11000111\n1010111000 11000111\n1010111001 11000111\n1010111010 11000111\n1010111011 11000111\n1010111100 11000111\n1010111101 11000111\n1010111110 11000111\n1010111111 11000111\n1011000000 11010111\n1011000001 11010111\n1011000010 11010111\n1011000011 11010111\n1011000100 11010111\n1011000101 11010111\n1011000110 11010111\n1011000111 11010111\n1011001000 11010111\n1011001001 11010111\n1011001010 11010111\n1011001011 11010111\n1011001100 11010111\n1011001101 11010111\n1011001110 11010111\n1011001111 11010111\n1011010000 11010111\n1011010001 11010111\n1011010010 11010111\n1011010011 11010111\n1011010100 11010111\n1011010101 11010111\n1011010110 11010111\n1011010111 11010111\n1011011000 11010111\n1011011001 11010111\n1011011010 11010111\n1011011011 11010111\n1011011100 11010111\n1011011101 11010111\n1011011110 11010111\n1011011111 11010111\n1011100000 11000111\n1011100001 11000111\n1011100010 11000111\n1011100011 11000111\n1011100100 11000111\n1011100101 11000111\n1011100110 11000111\n1011100111 11000111\n1011101000 11000111\n1011101001 11000111\n1011101010 11000111\n1011101011 11000111\n1011101100 11000111\n1011101101 11000111\n1011101110 11000111\n1011101111 11000111\n1011110000 11000111\n1011110001 11000111\n1011110010 11000111\n1011110011 11000111\n1011110100 11000111\n1011110101 11000111\n1011110110 11000111\n1011110111 11000111\n1011111000 11000111\n1011111001 11000111\n1011111010 11000111\n1011111011 11000111\n1011111100 11000111\n1011111101 11000111\n1011111110 11000111\n1011111111 11000111\n1100000000 11010111\n1100000001 11010111\n1100000010 11010111\n1100000011 11010111\n1100000100 11010111\n1100000101 11010111\n1100000110 11010111\n1100000111 11010111\n1100001000 11010111\n1100001001 11010111\n1100001010 11010111\n1100001011 11010111\n1100001100 11010111\n1100001101 11010111\n1100001110 11010111\n1100001111 11010111\n1100010000 11010111\n1100010001 11010111\n1100010010 11010111\n1100010011 11010111\n1100010100 11010111\n1100010101 11010111\n1100010110 11010111\n1100010111 11010111\n1100011000 11010111\n1100011001 11010111\n1100011010 11010111\n1100011011 11010111\n1100011100 11010111\n1100011101 11010111\n1100011110 11010111\n1100011111 11010111\n1100100000 11000111\n1100100001 11000111\n1100100010 11000111\n1100100011 11000111\n1100100100 11000111\n1100100101 11000111\n1100100110 11000111\n1100100111 11000111\n1100101000 11000111\n1100101001 11000111\n1100101010 11000111\n1100101011 11000111\n1100101100 11000111\n1100101101 11000111\n1100101110 11000111\n1100101111 11000111\n1100110000 11000111\n1100110001 11000111\n1100110010 11000111\n1100110011 11000111\n1100110100 11000111\n1100110101 11000111\n1100110110 11000111\n1100110111 11000111\n1100111000 11000111\n1100111001 11000111\n1100111010 11000111\n1100111011 11000111\n1100111100 11000111\n1100111101 11000111\n1100111110 11000111\n1100111111 11000111\n1101000000 11010111\n1101000001 11010111\n1101000010 11010111\n1101000011 11010111\n1101000100 11010111\n1101000101 11010111\n1101000110 11010111\n1101000111 11010111\n1101001000 11010111\n1101001001 11010111\n1101001010 11010111\n1101001011 11010111\n1101001100 11010111\n1101001101 11010111\n1101001110 11010111\n1101001111 11010111\n1101010000 11010111\n1101010001 11010111\n1101010010 11010111\n1101010011 11010111\n1101010100 11010111\n1101010101 11010111\n1101010110 11010111\n1101010111 11010111\n1101011000 11010111\n1101011001 11010111\n1101011010 11010111\n1101011011 11010111\n1101011100 11010111\n1101011101 11010111\n1101011110 11010111\n1101011111 11010111\n1101100000 11000111\n1101100001 11000111\n1101100010 11000111\n1101100011 11000111\n1101100100 11000111\n1101100101 11000111\n1101100110 11000111\n1101100111 11000111\n1101101000 11000111\n1101101001 11000111\n1101101010 11000111\n1101101011 11000111\n1101101100 11000111\n1101101101 11000111\n1101101110 11000111\n1101101111 11000111\n1101110000 11000111\n1101110001 11000111\n1101110010 11000111\n1101110011 11000111\n1101110100 11000111\n1101110101 11000111\n1101110110 11000111\n1101110111 11000111\n1101111000 11000111\n1101111001 11000111\n1101111010 11000111\n1101111011 11000111\n1101111100 11000111\n1101111101 11000111\n1101111110 11000111\n1101111111 11000111\n1110000000 11010111\n1110000001 11010111\n1110000010 11010111\n1110000011 11010111\n1110000100 11010111\n1110000101 11010111\n1110000110 11010111\n1110000111 11010111\n1110001000 11010111\n1110001001 11010111\n1110001010 11010111\n1110001011 11010111\n1110001100 11010111\n1110001101 11010111\n1110001110 11010111\n1110001111 11010111\n1110010000 11010111\n1110010001 11010111\n1110010010 11010111\n1110010011 11010111\n1110010100 11010111\n1110010101 11010111\n1110010110 11010111\n1110010111 11010111\n1110011000 11010111\n1110011001 11010111\n1110011010 11010111\n1110011011 11010111\n1110011100 11010111\n1110011101 11010111\n1110011110 11010111\n1110011111 11010111\n1110100000 11000111\n1110100001 11000111\n1110100010 11000111\n1110100011 11000111\n1110100100 11000111\n1110100101 11000111\n1110100110 11000111\n1110100111 11000111\n1110101000 11000111\n1110101001 11000111\n1110101010 11000111\n1110101011 11000111\n1110101100 11000111\n1110101101 11000111\n1110101110 11000111\n1110101111 11000111\n1110110000 11000111\n1110110001 11000111\n1110110010 11000111\n1110110011 11000111\n1110110100 11000111\n1110110101 11000111\n1110110110 11000111\n1110110111 11000111\n1110111000 11000111\n1110111001 11000111\n1110111010 11000111\n1110111011 11000111\n1110111100 11000111\n1110111101 11000111\n1110111110 11000111\n1110111111 11000111\n1111000000 11010111\n1111000001 11010111\n1111000010 11010111\n1111000011 11010111\n1111000100 11010111\n1111000101 11010111\n1111000110 11010111\n1111000111 11010111\n1111001000 11010111\n1111001001 11010111\n1111001010 11010111\n1111001011 11010111\n1111001100 11010111\n1111001101 11010111\n1111001110 11010111\n1111001111 11010111\n1111010000 11010111\n1111010001 11010111\n1111010010 11010111\n1111010011 11010111\n1111010100 11010111\n1111010101 11010111\n1111010110 11010111\n1111010111 11010111\n1111011000 11010111\n1111011001 11010111\n1111011010 11010111\n1111011011 11010111\n1111011100 11010111\n1111011101 11010111\n1111011110 11010111\n1111011111 11010111\n1111100000 11000111\n1111100001 11000111\n1111100010 11000111\n1111100011 11000111\n1111100100 11000111\n1111100101 11000111\n1111100110 11000111\n1111100111 11000111\n1111101000 11000111\n1111101001 11000111\n1111101010 11000111\n1111101011 11000111\n1111101100 11000111\n1111101101 11000111\n1111101110 11000111\n1111101111 11000111\n1111110000 11000111\n1111110001 11000111\n1111110010 11000111\n1111110011 11000111\n1111110100 11000111\n1111110101 11000111\n1111110110 11000111\n1111110111 11000111\n1111111000 11000111\n1111111001 11000111\n1111111010 11000111\n1111111011 11000111\n1111111100 11000111\n1111111101 11000111\n1111111110 11000111\n1111111111 11000111")) pla_3358 (
    .in({I9, I8, I7, I6, I5, I4, I3, I2, I1, I0}), .out({B7, B6, B5, B4, B3, B2, B1, B0}));
endmodule
