// Logisim project tektronix_ttl_symbols.circ as structural Verilog: 15 circuits, main circuit ttl_74393
module ttl_7474 (
  input  S,
  input  D,
  input  CLK,
  input  R,
  output Q,
  output NQ
);

  wire not_1_out, not_2_out;

  not not_1 (not_1_out, S);
  D_Flip_Flop d_ff_1 (.D(D), .clk(CLK), .Q(Q), .Qn(NQ), .preset(not_1_out), .reset(not_2_out));
  not not_2 (not_2_out, R);
endmodule

module ttl_74139 (
  input  G1,
  input  A1,
  input  B1,
  input  G2,
  input  A2,
  input  B2,
  output Y11,
  output Y12,
  output Y13,
  output Y14,
  output Y21,
  output Y22,
  output Y23,
  output Y24
);

  wire decoder_1_out0, decoder_1_out1, decoder_1_out2, decoder_1_out3, decoder_2_out0, decoder_2_out1,
       decoder_2_out2, decoder_2_out3, not_1_out, not_2_out;

  not not_1 (not_1_out, G1);
  not not_2 (not_2_out, G2);
  Decoder #(.select(2)) decoder_1 (
    .out0(decoder_1_out0), .out1(decoder_1_out1), .out2(decoder_1_out2), .out3(decoder_1_out3),
    .sel({B1, A1}), .en(not_1_out));
  Decoder #(.select(2)) decoder_2 (
    .out0(decoder_2_out0), .out1(decoder_2_out1), .out2(decoder_2_out2), .out3(decoder_2_out3),
    .sel({B2, A2}), .en(not_2_out));
  not not_3 (Y11, decoder_1_out0);
  not not_4 (Y12, decoder_1_out1);
  not not_5 (Y13, decoder_1_out2);
  not not_6 (Y14, decoder_1_out3);
  not not_7 (Y21, decoder_2_out0);
  not not_8 (Y22, decoder_2_out1);
  not not_9 (Y23, decoder_2_out2);
  not not_10 (Y24, decoder_2_out3);
endmodule

module ttl_74157 (
  input  SEL,
  input  A1,
  input  B1,
  input  STROBE,
  input  A2,
  input  B2,
  input  A3,
  input  B3,
  input  A4,
  input  B4,
  output Y1,
  output Y2,
  output Y3,
  output Y4
);

  wire not_1_out, not_2_out;

  not not_1 (not_1_out, SEL);
  not not_2 (not_2_out, STROBE);
  Multiplexer #(.enable("true")) multiplexer_1 (.in0(A1), .in1(B1), .out(Y1), .sel(not_1_out), .en(not_2_out));
  Multiplexer #(.enable("true")) multiplexer_2 (.in0(A2), .in1(B2), .out(Y2), .sel(not_1_out), .en(not_2_out));
  Multiplexer #(.enable("true")) multiplexer_3 (.in0(A3), .in1(B3), .out(Y3), .sel(not_1_out), .en(not_2_out));
  Multiplexer #(.enable("true")) multiplexer_4 (.in0(A4), .in1(B4), .out(Y4), .sel(not_1_out), .en(not_2_out));
endmodule

module ttl_74163 (
  input  ENT,
  input  ENP,
  input  CLR,
  input  LD,
  input  CLK,
  input  A,
  input  B,
  input  C,
  input  D,
  output RCO,
  output QA,
  output QB,
  output QC,
  output QD
);

  wire and_1_out, counter_1_carry, not_1_out, not_2_out;

  and and_1 (and_1_out, ENT, ENP);
  not not_1 (not_1_out, CLR);
  not not_2 (not_2_out, LD);
  Counter #(.max('hf), .width(4)) counter_1 (
    .clr(not_1_out), .load(not_2_out), .up(1'b1), .count(and_1_out), .clk(CLK), .D({D, C, B, A}),
    .carry(counter_1_carry), .Q({QD, QC, QB, QA}));
  and and_2 (RCO, ENT, counter_1_carry);
endmodule

module ttl_74166 (
  input  CLR,
  input  CLK,
  input  SH_LD,
  input  CLK_INH,
  input  SER,
  input  A,
  input  B,
  input  C,
  input  D,
  input  E,
  input  F,
  input  G,
  input  H,
  output QH
);

  wire and_1_out, not_1_out, not_2_out;

  and and_1 (and_1_out, CLK, ~CLK_INH);  // AND_Gate
  not not_1 (not_1_out, CLR);
  not not_2 (not_2_out, SH_LD);
  // Shift_Register shift_register_1: pin names not known; wires that end beside it: CLR, not_1_out, not_2_out, SH_LD, and_1_out, SER, A, B, C, D, E, F, G, H, QH
  // NoConnect on nothing
  // NoConnect on nothing
  // NoConnect on nothing
  // NoConnect on nothing
  // NoConnect on nothing
  // NoConnect on nothing
  // NoConnect on nothing
endmodule

module ttl_74175 (
  input  CLR,
  input  CLK,
  input  D1,
  input  D2,
  input  D3,
  input  D4,
  output Q1,
  output NQ1,
  output Q2,
  output NQ2,
  output Q3,
  output NQ3,
  output Q4,
  output NQ4
);

  wire not_1_out, undriven, undriven_2, undriven_3, undriven_4;

  not not_1 (not_1_out, CLR);
  D_Flip_Flop d_ff_1 (.D(D1), .clk(CLK), .Q(Q1), .Qn(NQ1), .preset(undriven), .reset(not_1_out));
  D_Flip_Flop d_ff_2 (.D(D2), .clk(CLK), .Q(Q2), .Qn(NQ2), .preset(undriven_2), .reset(not_1_out));
  D_Flip_Flop d_ff_3 (.D(D3), .clk(CLK), .Q(Q3), .Qn(NQ3), .preset(undriven_3), .reset(not_1_out));
  D_Flip_Flop d_ff_4 (.D(D4), .clk(CLK), .Q(Q4), .Qn(NQ4), .preset(undriven_4), .reset(not_1_out));
  // NoConnect on undriven
  // NoConnect on undriven_2
  // NoConnect on undriven_3
  // NoConnect on undriven_4
endmodule

module ttl_74244_joined (
  input  G,
  input  A1,
  input  A2,
  input  A3,
  input  A4,
  input  A5,
  input  A6,
  input  A7,
  input  A8,
  output Y1,
  output Y2,
  output Y3,
  output Y4,
  output Y5,
  output Y6,
  output Y7,
  output Y8
);

  wire not_1_out;

  not not_1 (not_1_out, G);
  assign {Y8, Y7, Y6, Y5, Y4, Y3, Y2, Y1} = not_1_out ? {A8, A7, A6, A5, A4, A3, A2, A1} : 8'bz;  // Controlled_Buffer controlled_buffer_1
endmodule

module ttl_74273 (
  input  CLR,
  input  CLK,
  input  D1,
  input  D2,
  input  D3,
  input  D4,
  input  D5,
  input  D6,
  input  D7,
  input  D8,
  output Q1,
  output Q2,
  output Q3,
  output Q4,
  output Q5,
  output Q6,
  output Q7,
  output Q8
);

  wire d_ff_1_qn, d_ff_2_qn, d_ff_3_qn, d_ff_4_qn, d_ff_5_qn, d_ff_6_qn, d_ff_7_qn, d_ff_8_qn, not_1_out,
       undriven, undriven_2, undriven_3, undriven_4, undriven_5, undriven_6, undriven_7, undriven_8;

  not not_1 (not_1_out, CLR);
  // NoConnect on undriven
  D_Flip_Flop d_ff_1 (.D(D1), .clk(CLK), .Q(Q1), .Qn(d_ff_1_qn), .preset(undriven), .reset(not_1_out));
  // NoConnect on undriven_2
  D_Flip_Flop d_ff_2 (.D(D2), .clk(CLK), .Q(Q2), .Qn(d_ff_2_qn), .preset(undriven_2), .reset(not_1_out));
  // NoConnect on undriven_3
  D_Flip_Flop d_ff_3 (.D(D3), .clk(CLK), .Q(Q3), .Qn(d_ff_3_qn), .preset(undriven_3), .reset(not_1_out));
  // NoConnect on undriven_4
  D_Flip_Flop d_ff_4 (.D(D4), .clk(CLK), .Q(Q4), .Qn(d_ff_4_qn), .preset(undriven_4), .reset(not_1_out));
  // NoConnect on undriven_5
  D_Flip_Flop d_ff_5 (.D(D5), .clk(CLK), .Q(Q5), .Qn(d_ff_5_qn), .preset(undriven_5), .reset(not_1_out));
  // NoConnect on undriven_6
  D_Flip_Flop d_ff_6 (.D(D6), .clk(CLK), .Q(Q6), .Qn(d_ff_6_qn), .preset(undriven_6), .reset(not_1_out));
  // NoConnect on undriven_7
  D_Flip_Flop d_ff_7 (.D(D7), .clk(CLK), .Q(Q7), .Qn(d_ff_7_qn), .preset(undriven_7), .reset(not_1_out));
  // NoConnect on undriven_8
  D_Flip_Flop d_ff_8 (.D(D8), .clk(CLK), .Q(Q8), .Qn(d_ff_8_qn), .preset(undriven_8));  // open: reset
  // NoConnect on d_ff_1_qn
  // NoConnect on d_ff_2_qn
  // NoConnect on d_ff_3_qn
  // NoConnect on d_ff_4_qn
  // NoConnect on d_ff_5_qn
  // NoConnect on d_ff_6_qn
  // NoConnect on d_ff_7_qn
  // NoConnect on d_ff_8_qn
endmodule

module ttl_74279_sr (
  input  S,
  input  R,
  output Q
);

  wire not_1_out, not_2_out, s_r_ff_1_qn, undriven, undriven_2;

  not not_1 (not_1_out, S);
  S_R_Flip_Flop #(.trigger("high")) s_r_ff_1 (
    .S(undriven), .R(undriven_2), .clk(1'b0), .Q(Q), .reset(not_2_out), .Qn(s_r_ff_1_qn), .preset(not_1_out));
  // NoConnect on undriven
  // NoConnect on undriven_2
  // NoConnect on s_r_ff_1_qn
  not not_2 (not_2_out, R);
endmodule

module ttl_74279_ssr (
  input  S1,
  input  S2,
  input  R,
  output Q
);

  wire not_1_out, or_1_out, s_r_ff_1_qn, undriven, undriven_2;

  not not_1 (not_1_out, R);
  or or_1 (or_1_out, ~S1, ~S2);  // OR_Gate
  S_R_Flip_Flop s_r_ff_1 (
    .S(undriven), .R(undriven_2), .clk(1'b0), .Q(Q), .reset(not_1_out), .Qn(s_r_ff_1_qn), .preset(or_1_out));
  // NoConnect on undriven
  // NoConnect on undriven_2
  // NoConnect on s_r_ff_1_qn
endmodule

module ttl_74283 (
  input  C0,
  input  A1,
  input  A2,
  input  A3,
  input  A4,
  input  B1,
  input  B2,
  input  B3,
  input  B4,
  output E1,
  output E2,
  output E3,
  output E4,
  output C4
);

  Adder #(.width(4)) adder_1 (.a({A4, A3, A2, A1}), .b({B4, B3, B2, B1}), .out({E4, E3, E2, E1}), .cin(C0), .cout(C4));
endmodule

module ttl_74374 (
  input  OC,
  input  CLK,
  input  D1,
  input  D2,
  input  D3,
  input  D4,
  input  D5,
  input  D6,
  input  D7,
  input  D8,
  output Q1,
  output Q2,
  output Q3,
  output Q4,
  output Q5,
  output Q6,
  output Q7,
  output Q8
);

  wire d_ff_1_q, d_ff_1_qn, d_ff_2_q, d_ff_2_qn, d_ff_3_q, d_ff_3_qn, d_ff_4_q, d_ff_4_qn, d_ff_5_q,
       d_ff_5_qn, d_ff_6_q, d_ff_6_qn, d_ff_7_q, d_ff_7_qn, d_ff_8_q, d_ff_8_qn, not_1_out, undriven,
       undriven_2, undriven_3, undriven_4, undriven_5, undriven_6, undriven_7, undriven_8, undriven_9,
       undriven_10, undriven_11, undriven_12, undriven_13, undriven_14, undriven_15, undriven_16;

  not not_1 (not_1_out, OC);
  // NoConnect on undriven
  D_Flip_Flop d_ff_1 (.D(D1), .clk(CLK), .Q(d_ff_1_q), .Qn(d_ff_1_qn), .preset(undriven), .reset(undriven_2));
  // NoConnect on d_ff_1_qn
  // NoConnect on undriven_2
  // NoConnect on undriven_3
  D_Flip_Flop d_ff_2 (.D(D2), .clk(CLK), .Q(d_ff_2_q), .Qn(d_ff_2_qn), .preset(undriven_3), .reset(undriven_4));
  // NoConnect on d_ff_2_qn
  // NoConnect on undriven_4
  // NoConnect on undriven_5
  D_Flip_Flop d_ff_3 (.D(D3), .clk(CLK), .Q(d_ff_3_q), .Qn(d_ff_3_qn), .preset(undriven_5), .reset(undriven_6));
  // NoConnect on d_ff_3_qn
  // NoConnect on undriven_6
  // NoConnect on undriven_7
  D_Flip_Flop d_ff_4 (.D(D4), .clk(CLK), .Q(d_ff_4_q), .Qn(d_ff_4_qn), .preset(undriven_7), .reset(undriven_8));
  // NoConnect on d_ff_4_qn
  // NoConnect on undriven_8
  // NoConnect on undriven_9
  D_Flip_Flop d_ff_5 (.D(D5), .clk(CLK), .Q(d_ff_5_q), .Qn(d_ff_5_qn), .preset(undriven_9), .reset(undriven_10));
  // NoConnect on d_ff_5_qn
  // NoConnect on undriven_10
  // NoConnect on undriven_11
  D_Flip_Flop d_ff_6 (.D(D6), .clk(CLK), .Q(d_ff_6_q), .Qn(d_ff_6_qn), .preset(undriven_11), .reset(undriven_12));
  // NoConnect on d_ff_6_qn
  // NoConnect on undriven_12
  // NoConnect on undriven_13
  D_Flip_Flop d_ff_7 (.D(D7), .clk(CLK), .Q(d_ff_7_q), .Qn(d_ff_7_qn), .preset(undriven_13), .reset(undriven_14));
  // NoConnect on d_ff_7_qn
  // NoConnect on undriven_14
  // NoConnect on undriven_15
  D_Flip_Flop d_ff_8 (.D(D8), .clk(CLK), .Q(d_ff_8_q), .Qn(d_ff_8_qn), .preset(undriven_15), .reset(undriven_16));
  // NoConnect on d_ff_8_qn
  // NoConnect on undriven_16
  assign Q1 = not_1_out ? d_ff_1_q : 1'bz;  // Controlled_Buffer controlled_buffer_1
  assign Q2 = not_1_out ? d_ff_2_q : 1'bz;  // Controlled_Buffer controlled_buffer_2
  assign Q3 = not_1_out ? d_ff_3_q : 1'bz;  // Controlled_Buffer controlled_buffer_3
  assign Q4 = not_1_out ? d_ff_4_q : 1'bz;  // Controlled_Buffer controlled_buffer_4
  assign Q5 = not_1_out ? d_ff_5_q : 1'bz;  // Controlled_Buffer controlled_buffer_5
  assign Q6 = not_1_out ? d_ff_6_q : 1'bz;  // Controlled_Buffer controlled_buffer_6
  assign Q7 = not_1_out ? d_ff_7_q : 1'bz;  // Controlled_Buffer controlled_buffer_7
  assign Q8 = not_1_out ? d_ff_8_q : 1'bz;  // Controlled_Buffer controlled_buffer_8
endmodule

module ttl_74393 (
  input  CLR_A,
  input  CLK_A,
  input  CLR_B,
  input  CLK_B,
  output QA0,
  output QA1,
  output QA2,
  output QA3,
  output QB0,
  output QB1,
  output QB2,
  output QB3
);

  wire counter_1_carry, counter_2_carry, not_1_out, not_2_out;

  not not_1 (not_1_out, CLK_A);
  not not_2 (not_2_out, CLK_B);
  Counter #(.max('hf), .width(4)) counter_1 (
    .clr(CLR_A), .load(1'b0), .up(1'b1), .count(1'b1), .clk(not_1_out), .D(4'b0000), .carry(counter_1_carry),
    .Q({QA3, QA2, QA1, QA0}));
  Counter #(.max('hf), .width(4)) counter_2 (
    .clr(CLR_B), .load(1'b0), .up(1'b1), .count(1'b1), .clk(not_2_out), .D(4'b0000), .carry(counter_2_carry),
    .Q({QB3, QB2, QB1, QB0}));
  // NoConnect on counter_1_carry
  // NoConnect on counter_2_carry
endmodule

module ttl_74670 (
  input  D1,
  input  GR,
  input  D2,
  input  D3,
  input  RA,
  input  D4,
  input  RB,
  input  WA,
  input  WB,
  input  GW,
  output Q1,
  output Q2,
  output Q3,
  output Q4
);

  wire decoder_1_out0, decoder_1_out1, decoder_1_out2, decoder_1_out3, not_1_out;
  wire [3:0] register_1_q, register_2_q, register_3_q, register_4_q;

  Decoder #(.enable("false"), .select(2)) decoder_1 (
    .out0(decoder_1_out0), .out1(decoder_1_out1), .out2(decoder_1_out2), .out3(decoder_1_out3), .sel({WB, WA}));
  Register #(.trigger("low"), .width(4)) register_1 (
    .D({D4, D3, D2, D1}), .en(decoder_1_out0), .clk(GW), .Q(register_1_q), .clr(1'b0));
  Register #(.trigger("low"), .width(4)) register_2 (
    .D({D4, D3, D2, D1}), .en(decoder_1_out1), .clk(GW), .Q(register_2_q), .clr(1'b0));
  Register #(.trigger("low"), .width(4)) register_3 (
    .D({D4, D3, D2, D1}), .en(decoder_1_out2), .clk(GW), .Q(register_3_q), .clr(1'b0));
  Register #(.trigger("low"), .width(4)) register_4 (
    .D({D4, D3, D2, D1}), .en(decoder_1_out3), .clk(GW), .Q(register_4_q), .clr(1'b0));
  not not_1 (not_1_out, GR);
  Multiplexer #(.disabled("Z"), .enable("true"), .select(2), .width(4)) multiplexer_1 (
    .in0(register_1_q), .in1(register_2_q), .in2(register_3_q), .in3(register_4_q), .out({Q4, Q3, Q2, Q1}),
    .sel({RB, RA}), .en(not_1_out));
endmodule

module mem_6116P_2 (
  input  A0,
  input  A1,
  input  WE,
  input  A2,
  input  OE,
  input  A3,
  input  CS,
  input  A4,
  input  ID0,
  input  A5,
  input  ID1,
  input  A6,
  input  ID2,
  input  A7,
  input  ID3,
  input  A8,
  input  ID4,
  input  A9,
  input  ID5,
  input  A10,
  input  ID6,
  input  ID7,
  output OD0,
  output OD1,
  output OD2,
  output OD3,
  output OD4,
  output OD5,
  output OD6,
  output OD7
);

  wire not_1_out, not_2_out, not_3_out;

  RAM #(.addrWidth(11)) ram_1 (
    .addr({A10, A9, A8, A7, A6, A5, A4, A3, A2, A1, A0}), .we(not_1_out), .oe(not_2_out), .clk(not_3_out),
    .din({ID7, ID6, ID5, ID4, ID3, ID2, ID1, ID0}), .dout({OD7, OD6, OD5, OD4, OD3, OD2, OD1, OD0}));
  not not_1 (not_1_out, WE);
  not not_2 (not_2_out, OE);
  not not_3 (not_3_out, CS);
endmodule
